# Fritzing sketch sd_logging_schematic (saved by Fritzing 0.9.3b)
circuit board: 8.45767cm x 5.75246cm

parts:
  Part1 = Adafruit HUZZAH32 ESP32 Feather [part_number="Adafruit #3405"]
  Part2 = Adafruit MicroSD card breakout board [part_number="Adafruit #254"]
  Part3 = Adafruit LSM303DLHC Triple-axis Accelerometer+Magnetometer (Compass) [part_number="Adafruit #1120"]

nets:
  N1: Part1.MISO, Part2.DO
  N2: Part1.MOSI, Part2.DI
  N3: Part1.SCK, Part2.CLK
  N4: Part1.A5_IO4, Part2.CS
  GND: Part1.GND, Part2.GND, Part3.GND
  3.3V: Part1.3.3V, Part2.VCC, Part3.VIN
  N5: Part1.SCL, Part3.SCL
  N6: Part1.SDA, Part3.SDA

custom parts:
  Adafruit MicroSD card breakout board: Not just a simple breakout board, this microSD adapter goes the extra mile - designed for ease of use. Onboard 5v->3v regulator provides 150mA for power-hungry cards 3v level shifting means you can use this with ease on either 3v or 5v systems Uses a proper level shifting chip, not resistors: less problems, and faster read/write access Use 3 or 4 digital pins to read and write 2Gb+ of storage!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
  Adafruit LSM303DLHC Triple-axis Accelerometer+Magnetometer (Compass): He told you "Go West, young maker!" - but you don't know which way is West! Ah, if only you had this triple-axis accelerometer/magnetometer compass module. Inside are two sensors, one is a classic 3-axis accelerometer, which can tell you which direction is down towards the Earth (by measuring gravity). The other is a magnetometer that can sense where the strongest magnetic force is coming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
